# Fritzing sketch sketch-02 (saved by Fritzing 0.9.3b)
breadboards: 1

parts:
  LCD1 = LCD screen
  U1 = POT [package=pot_mammoth]
  Componente1 = Arduino Mega 2560 (Rev3)
  Keypad4x1 = Keypad Membran 4x4
  U2 = L6470 [package=htssop28]
  M1 = Stepper Motor - Unipolar  # not connected

nets:
  VSS: LCD1.VSS, LCD1.R/W, LCD1.LED-, U1.E, Componente1.GND, U2.OUT1A
  VDD: LCD1.VDD, LCD1.LED+, U1.S, Componente1.5V, U2.VSA
  N1: LCD1.V0, U1.A
  N2: LCD1.RS, Componente1.D1_TX0
  N3: LCD1.E, Componente1.D2_PWM
  N4: LCD1.DB4, Componente1.D4_PWM
  N5: LCD1.DB5, Componente1.D5_PWM
  N6: LCD1.DB6, Componente1.D6_PWM
  N7: LCD1.DB7, Componente1.D7_PWM
  N8: Componente1.D21/SCL, Keypad4x1.Pin1
  N9: Componente1.D20/SDA, Keypad4x1.Pin2
  N10: Componente1.D19/RX1, Keypad4x1.Pin3
  N11: Componente1.D18/TX1, Keypad4x1.Pin4
  N12: Componente1.D17_PWM/RX2, Keypad4x1.Pin5
  N13: Componente1.D16_PWM/TX2, Keypad4x1.Pin6
  N14: Componente1.D15/RX3, Keypad4x1.Pin7
  N15: Componente1.D14/TX3, Keypad4x1.Pin8
  N16: Componente1.D11_PWM, U2.VSA2
  N17: Componente1.D10_PWM, U2.PGNDA
  N18: Componente1.D9_PWM, U2.OUT2A
  N19: Componente1.D8_PWM, U2.EPAD

custom parts:
  Keypad Membran 4x4: Membrane Keypad 4x4 Matrix
